# Fritzing sketch DoorbellLock (saved by Fritzing 0.9.3b)
circuit board: 6.01157cm x 4.61945cm
perfboards: 1

parts:
  WeMos_D1_Mini1 = WeMos D1 Mini
  RFID = female pin header, 4 pins [form="♀ (female)"]
  DoorBell_Button = female pin header, 5 pins [form="♀ (female)"]
  Mail = female pin header, 3 pins [form="♀ (female)"]
  DoorBell_Relay = female pin header, 3 pins [form="♀ (female)"]
  Lock = female pin header, 3 pins [form="♀ (female)"]
  Lock_2 = female pin header, 2 pins [form="♀ (female)"]
  Door = female pin header, 2 pins [form="♀ (female)"]
  R1 = Resistor [tolerance=±5% resistance=220 package=THT]
  Power = Screw terminal - 2 pins [package=THT]
  Reset = male pin header, 2 pins [form="♂ (male)"]
  Indicator = LED - 5mm [color="Red (633nm)" package="5 mm [THT]"]
  C1 = Electrolytic Capacitor [capacitance=1µF package="100 mil [THT, electrolytic]"]
  R2 = Resistor [tolerance=±5% resistance=220 package=THT]

nets:
  N1: WeMos_D1_Mini1.3V3, Mail.pin1, R2.Pin_0
  N2: WeMos_D1_Mini1.5V, RFID.pin2, DoorBell_Relay.pin1, Lock.pin1, Power.pin1, C1.+
  N3: WeMos_D1_Mini1.A0, Mail.pin2
  N4: WeMos_D1_Mini1.D0, DoorBell_Button.pin4
  N5: WeMos_D1_Mini1.D1, Lock.pin3
  N6: WeMos_D1_Mini1.D2, Lock_2.pin2, R2.Pin_1
  N7: WeMos_D1_Mini1.D3, Door.pin2
  N8: WeMos_D1_Mini1.D4, DoorBell_Button.pin1
  N9: WeMos_D1_Mini1.D5, DoorBell_Button.pin3
  N10: WeMos_D1_Mini1.D6, DoorBell_Button.pin2
  N11: WeMos_D1_Mini1.D7, DoorBell_Relay.pin3
  N12: WeMos_D1_Mini1.D8, R1.Pin_0
  N13: WeMos_D1_Mini1.G, RFID.pin1, DoorBell_Button.pin5, Mail.pin3, DoorBell_Relay.pin2, Lock.pin2, Lock_2.pin1, Door.pin1, Power.pin2, Reset.pin2, Indicator.cathode, C1.-
  N14: WeMos_D1_Mini1.RST, Reset.pin1
  N15: WeMos_D1_Mini1.RX, RFID.pin3
  N16: WeMos_D1_Mini1.TX, RFID.pin4
  N17: R1.Pin_1, Indicator.anode

notes:
  Sensors
  +
